# Fritzing sketch morse_encoder (saved by Fritzing 0.9.3b)
breadboards: 1

parts:
  Part1 = Arduino Uno (Rev3) - ICSP
  LED2 = LED - 5mm [color="Yellow (595nm)" part_number=OUT_PIN package="5 mm [THT]"]
  LED3 = LED - 5mm [color="Red (633nm)" part_number=END_PIN package="5 mm [THT]"]
  R1 = Resistor [tolerance=±5% resistance=220 package=THT]
  R2 = Resistor [tolerance=±5% resistance=220 package=THT]
  K1 = Relay [part_number=FRS1B-S package=THT]
  K2 = Relay [part_number=FRS1B-S package=THT]

nets:
  N1: Part1.5V, K1.A, K1.COIL1, K2.COIL1, K2.B
  N2: Part1.D8, R2.Pin_0, K1.C1, K1.C2
  N3: Part1.GND, LED2.cathode, LED3.cathode, K1.COIL2, K2.COIL2
  N4: Part1.D7, R1.Pin_0, K2.C1, K2.C2
  N5: LED2.anode, R2.Pin_1
  N6: LED3.anode, R1.Pin_1

custom parts:
  Relay: An SPDT relay.
